// Logisim project BPU.circ as structural Verilog: 13 circuits, main circuit main
module main (
  input  [7:0] Input
);

  wire AND_2_out, AND_out, bpu_1_d__mem, bpu_1_direction_select__neg, bpu_1_i_o, bpu_1_mem__d, clock_1_out,
       Confirm_out, display_driver_1_ready, load_signal_generator_1_load, n0_flag_1_is_zero, not_1_out,
       OR_out, Reset_out;
  wire [3:0] display_driver_1_high_nibble, display_driver_1_low_nibble;
  wire [4:0] bpu_1_i_o_argument;
  wire [7:0] bpu_1_address_out, bpu_1_data_out, ram_1_data, rom_1_data;

  // Probe on bpu_1_address_out
  Load_signal_generator load_signal_generator_1 (
    .Clock(clock_1_out), .Adress_bus(bpu_1_address_out), .Reset(Reset_out),
    .Load(load_signal_generator_1_load));
  RAM #(.bus("separate")) ram_1 (
    .addr(bpu_1_address_out), .din(bpu_1_data_out), .data(ram_1_data), .str(bpu_1_d__mem), .sel(1'b1),
    .clk(clock_1_out), .ld(1'b1), .clr(Reset_out));
  ROM rom_1 (.addr(bpu_1_address_out), .data(rom_1_data), .sel(load_signal_generator_1_load));
  assign rom_1_data = bpu_1_mem__d ? ram_1_data : 8'bz;  // Controlled_Buffer controlled_buffer_1
  _0_Flag u_0_flag_1 (.Data(ram_1_data), .Is_zero(n0_flag_1_is_zero));
  BPU bpu_1 (
    .Address_Out(bpu_1_address_out), ._0(n0_flag_1_is_zero), .Data_In(rom_1_data), .Data_Out(bpu_1_data_out),
    .Clock(clock_1_out), .Reset(Reset_out), .I_O(bpu_1_i_o),
    .Direction_select__NEG(bpu_1_direction_select__neg), .I_O_argument(bpu_1_i_o_argument),
    .MEM__D(bpu_1_mem__d), .D__MEM(bpu_1_d__mem), .Load(load_signal_generator_1_load), .Resume(OR_out));
  Clock clock_1 (.out(clock_1_out));
  // Probe on bpu_1_data_out
  or OR (OR_out, display_driver_1_ready, Confirm_out);
  Button Reset (.out(Reset_out));
  // Probe on bpu_1_i_o_argument
  not not_1 (not_1_out, bpu_1_direction_select__neg);
  Hex_Digit_Display hex_digit_display_1 (.value(display_driver_1_high_nibble));  // open: dp
  Hex_Digit_Display hex_digit_display_2 (.value(display_driver_1_low_nibble));  // open: dp
  assign rom_1_data = AND_out ? Input : 8'bz;  // Controlled_Buffer controlled_buffer_2
  and AND (AND_out, bpu_1_i_o, not_1_out);
  and AND_2 (AND_2_out, bpu_1_i_o, bpu_1_direction_select__neg);
  Display_driver display_driver_1 (
    .Data_in(bpu_1_data_out), .Reset(Reset_out), .Clock(clock_1_out), .Enable(AND_2_out),
    .Ready(display_driver_1_ready), .High_nibble(display_driver_1_high_nibble),
    .Low_nibble(display_driver_1_low_nibble));
  Button Confirm (.out(Confirm_out));
  LED Input_request (.in(AND_out));

  // Notes on the sheet:
  //   contents of rom_1 (hex, n*v repeats v):
  //   72 fa 6 2 14 1 5 2 14 1 5 45 0 b dc 2 2c a 0 b 1 1d 2 3c 3 0 a 0 3 1 2d 2 2c 3 0 2 1 1d 13 1 cd ed a
  //   7 b 0 25
endmodule

module BPU_Layout (
  input  [7:0] Data_In,
  output [7:0] Address_Out,
  output [7:0] Data_Out
);


  assign Address_Out = Data_In;
  assign Data_Out = Data_In;

  // Notes on the sheet:
  //   Data
  //   Pointer
  //   Program
  //   Counter
  //   Arithmetic and Logic
  //   Unit
  //   Program
  //   Register
  //   Command
  //   decoder
endmodule

module BPU (
  input  Reset,
  input  _0,
  input  [7:0] Data_In,
  input  Clock,
  input  Resume,
  input  Load,
  output [7:0] Address_Out,
  output MEM__D,
  output D__MEM,
  output [7:0] Data_Out,
  output I_O,
  output [4:0] I_O_argument,
  output Direction_select__NEG
);

  wire AND_2_out, AND_3_out, AND_4_out, AND_5_out, AND_6_out, AND_out, command_decoder_shifter_1_alu__d,
       command_decoder_shifter_1_d__dp, command_decoder_shifter_1_d__pc, command_decoder_shifter_1_d__pr,
       command_decoder_shifter_1_dp__a, command_decoder_shifter_1_dp__d, command_decoder_shifter_1_i_o,
       command_decoder_shifter_1_pc__a, command_decoder_shifter_1_pc__d,
       command_decoder_shifter_1_pc_plus_plus, not_1_out, not_2_out, not_3_out, OR_out, XOR_out;
  wire [2:1] register_2_q;
  wire [7:0] alu_1_data_2, counter_1_q, register_1_q;

  assign Address_Out = command_decoder_shifter_1_dp__a ? register_1_q : 8'bz;  // Controlled_Buffer controlled_buffer_1
  and AND (AND_out, XOR_out, command_decoder_shifter_1_d__pc);
  assign Address_Out = command_decoder_shifter_1_pc__a ? counter_1_q : 8'bz;  // Controlled_Buffer controlled_buffer_2
  Register register_1 (
    .D(Data_In), .en(command_decoder_shifter_1_d__dp), .Q(register_1_q), .clk(AND_2_out), .clr(Reset));
  assign Data_In = command_decoder_shifter_1_dp__d ? register_1_q : 8'bz;  // Controlled_Buffer controlled_buffer_3
  xor XOR (XOR_out, Direction_select__NEG, _0);
  Counter counter_1 (
    .load(AND_out), .D(Data_In), .count(command_decoder_shifter_1_pc_plus_plus), .Q(counter_1_q),
    .clk(AND_2_out), .clr(Reset));  // open: carry
  assign Data_In = command_decoder_shifter_1_pc__d ? counter_1_q : 8'bz;  // Controlled_Buffer controlled_buffer_4
  Register register_2 (
    .D(Data_In), .en(command_decoder_shifter_1_d__pr),
    .Q({I_O_argument, register_2_q, Direction_select__NEG}), .clk(AND_2_out));  // open: clr
  assign Data_In = command_decoder_shifter_1_alu__d ? alu_1_data_2 : 8'bz;  // Controlled_Buffer controlled_buffer_5
  // Probe on {register_2_q, Direction_select__NEG}
  Command_Decoder__Shifter command_decoder_shifter_1 (
    .D__PR(command_decoder_shifter_1_d__pr), .ALU__D(command_decoder_shifter_1_alu__d), .D__MEM(D__MEM),
    .MEM__D(MEM__D), .D__DP(command_decoder_shifter_1_d__dp), .DP__D(command_decoder_shifter_1_dp__d),
    .DP__A(command_decoder_shifter_1_dp__a), .D__PC(command_decoder_shifter_1_d__pc),
    .PC_plus_plus(command_decoder_shifter_1_pc_plus_plus), .PC__A(command_decoder_shifter_1_pc__a),
    .PC__D(command_decoder_shifter_1_pc__d), .I_O(command_decoder_shifter_1_i_o),
    .Command({register_2_q, Direction_select__NEG}), .Clock(AND_2_out), .Reset(Reset), .Load(Load));
  and AND_2 (AND_2_out, Clock, OR_out);
  ALU alu_1 (
    .Argument(I_O_argument), .Data(Data_In), .D__ALU(1'b1), .Clock(AND_2_out), .Data_2(alu_1_data_2),
    .NEG(Direction_select__NEG));
  not not_1 (not_1_out, command_decoder_shifter_1_i_o);
  or OR (OR_out, AND_5_out, Reset, AND_6_out);
  not not_2 (not_2_out, OR_out);
  and AND_3 (AND_3_out, not_2_out, not_3_out);
  and AND_4 (AND_4_out, command_decoder_shifter_1_i_o, I_O);
  and AND_5 (AND_5_out, OR_out, not_1_out);
  and AND_6 (AND_6_out, Resume, I_O);
  or OR_2 (I_O, AND_3_out, AND_4_out);
  not not_3 (not_3_out, Resume);

  assign Data_Out = Data_In;
endmodule

module Command_Decoder__Shifter (
  input  [2:0] Command,
  input  Clock,
  input  Reset,
  input  Load,
  output D__PR,
  output ALU__D,
  output D__MEM,
  output MEM__D,
  output I_O,
  output D__DP,
  output DP__D,
  output DP__A,
  output D__PC,
  output PC__D,
  output PC__A,
  output PC_plus_plus
);

  wire AND_2_out, AND_3_out, AND_4_out, AND_5_out, AND_out, not_1_out, not_2_out, not_3_out, OR_out,
       shift_register_1_q0;

  not not_1 (not_1_out, Command[2]);
  not not_2 (not_2_out, Command[1]);
  not not_3 (not_3_out, Clock);
  nor NOR (D__PR, shift_register_1_q0, Load, ALU__D);
  Shift_Register #(.length(2)) shift_register_1 (
    .shift(1'b1), .in(D__PR), .clk(not_3_out), .clr(OR_out), .q0(shift_register_1_q0), .q1(ALU__D));  // open: out, load, d0, d1
  or OR (OR_out, Reset, AND_out, Load);
  and AND (AND_out, ALU__D, Command[1], Command[2]);
  and AND_2 (AND_2_out, not_2_out, not_1_out);
  and AND_3 (AND_3_out, Command[1], Command[2]);
  and AND_4 (AND_4_out, shift_register_1_q0, not_2_out, not_1_out);
  and AND_5 (AND_5_out, shift_register_1_q0, Command[0], Command[1], Command[2]);
  and AND_6 (I_O, shift_register_1_q0, Command[1], Command[2]);
  and AND_7 (D__DP, ALU__D, Command[1]);
  and AND_8 (DP__D, shift_register_1_q0, Command[1], not_1_out);
  or OR_2 (DP__A, ALU__D, shift_register_1_q0);
  and AND_9 (D__PC, ALU__D, Command[2]);
  and AND_10 (PC__D, shift_register_1_q0, not_2_out, Command[2]);
  or OR_3 (PC__A, Load, D__PR);
  or OR_4 (PC_plus_plus, Load, shift_register_1_q0);
  or OR_5 (D__MEM, AND_2_out, Load, AND_3_out);
  or OR_6 (MEM__D, AND_4_out, D__PR, AND_5_out);
endmodule

module Command_Decoder__Counter__suboptimal (
  input  Reset,
  input  Clock,
  input  Load,
  input  [2:0] Command,
  output D__PR,
  output ALU__D,
  output D__MEM,
  output MEM__D,
  output I_O,
  output D__DP,
  output DP__D,
  output DP__A,
  output D__PC,
  output PC__D,
  output PC_plus_plus,
  output PC__A
);

  wire AND_2_out, AND_5_out, AND_6_out, AND_7_out, AND_8_out, AND_9_out, AND_10_out, AND_out, not_1_out,
       not_2_out, not_3_out, not_4_out, not_5_out, OR_2_out, OR_3_out, OR_out;
  wire [1:0] counter_1_q;

  not not_1 (not_1_out, Clock);
  Counter #(.width(2), .max('h3)) counter_1 (
    .count(1'b1), .Q(counter_1_q), .clk(not_1_out), .clr(OR_out));  // open: load, D, carry
  or OR (OR_out, Reset, AND_out, AND_2_out);
  or OR_2 (OR_2_out, Load, counter_1_q[0]);
  or OR_3 (OR_3_out, counter_1_q[1], Load);
  not not_2 (not_2_out, OR_2_out);
  and AND (AND_out, OR_2_out, OR_3_out);
  not not_3 (not_3_out, OR_3_out);
  not not_4 (not_4_out, Command[2]);
  not not_5 (not_5_out, Command[1]);
  and AND_2 (AND_2_out, Command[1], Command[2], not_3_out, OR_2_out);
  and AND_3 (D__PR, not_3_out, not_2_out);
  and AND_4 (ALU__D, OR_2_out, not_3_out);
  and AND_5 (AND_5_out, OR_3_out, OR_3_out);
  and AND_6 (AND_6_out, not_5_out, not_4_out);
  or OR_4 (D__MEM, AND_5_out, AND_6_out, AND_7_out);
  and AND_7 (AND_7_out, Command[1], Command[2]);
  and AND_8 (AND_8_out, not_2_out, not_3_out);
  or OR_5 (MEM__D, AND_8_out, AND_9_out, AND_10_out);
  and AND_9 (AND_9_out, not_5_out, not_4_out, not_2_out);
  and AND_10 (AND_10_out, Command[0], Command[1], Command[2], not_2_out);
  and AND_11 (I_O, Command[1], Command[2], not_2_out, OR_3_out);
  and AND_12 (D__DP, Command[1], not_3_out, OR_2_out);
  and AND_13 (DP__D, Command[1], not_4_out, not_2_out, OR_3_out);
  xor XOR (DP__A, OR_3_out, OR_2_out);
  and AND_14 (D__PC, Command[2], not_3_out, OR_2_out);
  and AND_15 (PC__D, not_5_out, Command[2], OR_3_out, not_2_out);
  xor XOR_2 (PC__A, not_3_out, OR_2_out);

  assign PC_plus_plus = PC__A;
endmodule

module ALU (
  input  [4:0] Argument,
  input  [7:0] Data,
  input  D__ALU,
  input  Clock,
  input  NEG,
  output [7:0] Data_2
);

  wire [7:0] adder_1_out, register_1_q, XOR_out;

  Register register_1 (.D(Data), .en(D__ALU), .Q(register_1_q), .clk(Clock));  // open: clr
  assign XOR_out = {8{NEG}} ^ register_1_q;  // XOR_Gate XOR, 8 bits wide
  Adder adder_1 (.a({3'b000, Argument}), .b(XOR_out), .out(adder_1_out), .cin(1'b1));  // open: cout
  assign Data_2 = adder_1_out ^ {8{NEG}};  // XOR_Gate XOR_2, 8 bits wide
endmodule

module Display_driver (
  input  [7:0] Data_in,
  input  Reset,
  input  Clock,
  input  Enable,
  output [3:0] High_nibble,
  output [3:0] Low_nibble,
  output Ready
);

  wire not_1_out;

  not not_1 (not_1_out, Enable);
  Register register_1 (.D(Data_in), .en(Enable), .Q({High_nibble, Low_nibble}), .clk(Clock), .clr(Reset));
  D_Flip_Flop d_ff_1 (.clk(Clock), .D(Enable), .Q(Ready), .preset(1'b0), .en(1'b1), .reset(not_1_out));  // open: Qn
endmodule

module _0_Flag (
  input  [7:0] Data,
  output Is_zero
);

  nor NOR (Is_zero, Data[0], Data[1], Data[2], Data[3], Data[5], Data[6], Data[7], Data[4]);
endmodule

module Load_signal_generator (
  input  Clock,
  input  [7:0] Adress_bus,
  input  Reset,
  output Load
);

  wire nor_1_out, not_1_out, not_2_out, s_r_ff_1_q;

  not not_1 (not_1_out, Clock);
  nor nor_1 (nor_1_out, Adress_bus[0], Adress_bus[1], Adress_bus[2], Adress_bus[3], Adress_bus[5], Adress_bus[6], Adress_bus[7], Adress_bus[4]);
  S_R_Flip_Flop s_r_ff_1 (
    .S(1'b0), .clk(Clock), .R(not_2_out), .Q(s_r_ff_1_q), .preset(Reset), .en(1'b1));  // open: Qn, reset
  not not_2 (not_2_out, Reset);
  S_R_Flip_Flop s_r_ff_2 (
    .S(1'b0), .clk(not_1_out), .R(nor_1_out), .Q(Load), .preset(s_r_ff_1_q), .en(1'b1));  // open: Qn, reset
endmodule

module Simple_showcases (
  input  [7:0] B,
  input  in,
  input  [7:0] Address_bus,
  input  [7:0] A,
  input  NEG,
  input  [7:0] Input,
  input  Reset,
  input  Clock,
  input  Next_Command,
  input  [7:0] Data_bus,
  input  Clock_2,
  input  Resume,
  input  Reset_2,
  input  D__ALU,
  input  NEG_2,
  input  Load,
  input  [4:0] Argument,
  input  ALU__D,
  input  Wait,
  output [7:0] A_____B,
  output out_21,
  output BPU_clock,
  output _0,
  output _1,
  output _2,
  output L
);

  wire clock_1_out, clock_2_out, Confirm_out, load_signal_generator_1_load, not_1_out, not_2_out, OR_2_out,
       OR_out;
  wire [7:0] adder_1_out, alu_1_data_2, controlled_buffer_1_out, rom_1_data, XOR_out;

  Clock clock_1 (.out(clock_1_out));
  Load_signal_generator load_signal_generator_1 (
    .Clock(clock_1_out), .Adress_bus(Address_bus), .Reset(Reset), .Load(load_signal_generator_1_load));
  not not_1 (not_1_out, Wait);
  or OR (OR_out, Resume, not_1_out);
  // Probe on rom_1_data
  ROM rom_1 (.addr(Address_bus), .data(rom_1_data), .sel(load_signal_generator_1_load));
  // Probe on load_signal_generator_1_load
  and AND (BPU_clock, Clock, OR_out);
  LED Input_request (.in(in));
  assign controlled_buffer_1_out = in ? Input : 8'bz;  // Controlled_Buffer controlled_buffer_1
  Button Confirm (.out(Confirm_out));
  Clock u_clock_2 (.out(clock_2_out));
  // Probe on controlled_buffer_1_out
  assign Data_bus = ALU__D ? alu_1_data_2 : 8'bz;  // Controlled_Buffer controlled_buffer_2
  // Probe on alu_1_data_2
  ALU alu_1 (
    .Argument(Argument), .Data(Data_bus), .D__ALU(D__ALU), .Clock(clock_2_out), .Data_2(alu_1_data_2),
    .NEG(NEG_2));
  // Probe on Confirm_out
  not not_2 (not_2_out, Clock_2);
  nor NOR (_0, _1, Load, _2);
  assign XOR_out = A ^ {8{NEG}};  // XOR_Gate XOR, 8 bits wide
  Shift_Register #(.length(2)) shift_register_1 (
    .shift(1'b1), .in(_0), .clk(not_2_out), .clr(OR_2_out), .q0(_1), .q1(_2));  // open: out, load, d0, d1
  Adder adder_1 (.a(B), .b(XOR_out), .out(adder_1_out));  // open: cin, cout
  or OR_2 (OR_2_out, Next_Command, Reset_2, Load);
  assign A_____B = adder_1_out ^ {8{NEG}};  // XOR_Gate XOR_2, 8 bits wide

  assign L = Load;

  // Notes on the sheet:
  //   ROM
  //   Clock logic
  //   Input
  //   ALU
  //   Add/subtract
  //   Cycle Counter
endmodule

module Register_showcases (
  input  D__DP,
  input  [7:0] Data_bus,
  input  DP__D,
  input  D__PR,
  input  DP__A,
  input  NEG,
  input  _0,
  input  D__PC,
  input  PC_plus_plus,
  input  PC__D,
  input  PC__A
);

  wire AND_out, clock_1_out, clock_2_out, clock_3_out, Reset_2_out, Reset_out, XOR_out;
  wire [7:0] controlled_buffer_1_out, controlled_buffer_2_out, controlled_buffer_3_out,
       controlled_buffer_4_out, counter_1_q, register_1_q, register_2_q;

  // Probe on controlled_buffer_1_out
  assign controlled_buffer_1_out = DP__A ? register_1_q : 8'bz;  // Controlled_Buffer controlled_buffer_1
  Register register_1 (.D(controlled_buffer_2_out), .en(D__DP), .Q(register_1_q), .clk(clock_1_out), .clr(Reset_out));
  Clock clock_1 (.out(clock_1_out));
  Button Reset (.out(Reset_out));
  xor XOR (XOR_out, NEG, _0);
  // Probe on controlled_buffer_3_out
  // Probe on controlled_buffer_2_out
  assign controlled_buffer_2_out = DP__D ? register_1_q : 8'bz;  // Controlled_Buffer controlled_buffer_2
  and AND (AND_out, XOR_out, D__PC);
  assign controlled_buffer_3_out = PC__A ? counter_1_q : 8'bz;  // Controlled_Buffer controlled_buffer_3
  Clock clock_2 (.out(clock_2_out));
  Counter counter_1 (
    .load(AND_out), .D(controlled_buffer_4_out), .count(PC_plus_plus), .Q(counter_1_q), .clk(clock_2_out),
    .clr(Reset_2_out));  // open: carry
  // Probe on controlled_buffer_4_out
  assign controlled_buffer_4_out = PC__D ? counter_1_q : 8'bz;  // Controlled_Buffer controlled_buffer_4
  Button Reset_2 (.out(Reset_2_out));
  Clock clock_3 (.out(clock_3_out));
  // Probe on register_2_q[7:3]
  Register register_2 (.D(Data_bus), .en(D__PR), .Q(register_2_q), .clk(clock_3_out));  // open: clr
  // Probe on register_2_q[0]
  // Probe on register_2_q[2:0]

  // Notes on the sheet:
  //   Data pointer
  //   Program counter
  //   Program register
endmodule

module RAM_showcase (
  input  [7:0] Address_bus,
  input  MEM__D,
  input  D__MEM
);

  wire clock_1_out, n0_flag_1_is_zero, Reset_out;
  wire [7:0] controlled_buffer_1_out, ram_1_data;

  Clock clock_1 (.out(clock_1_out));
  RAM #(.bus("separate")) ram_1 (
    .addr(Address_bus), .din(controlled_buffer_1_out), .data(ram_1_data), .str(D__MEM), .sel(1'b1),
    .clk(clock_1_out), .ld(1'b1), .clr(Reset_out));
  Button Reset (.out(Reset_out));
  // Probe on controlled_buffer_1_out
  assign controlled_buffer_1_out = MEM__D ? ram_1_data : 8'bz;  // Controlled_Buffer controlled_buffer_1
  // Probe on n0_flag_1_is_zero
  _0_Flag u_0_flag_1 (.Data(ram_1_data), .Is_zero(n0_flag_1_is_zero));
endmodule

module Output_showcase (
  input  [7:0] Data_bus,
  input  Output_flag
);

  wire clock_1_out, display_driver_1_ready, Reset_out;
  wire [3:0] display_driver_1_high_nibble, display_driver_1_low_nibble;

  Hex_Digit_Display hex_digit_display_1 (.value(display_driver_1_high_nibble));  // open: dp
  Clock clock_1 (.out(clock_1_out));
  Hex_Digit_Display hex_digit_display_2 (.value(display_driver_1_low_nibble));  // open: dp
  Display_driver display_driver_1 (
    .Data_in(Data_bus), .Reset(Reset_out), .Clock(clock_1_out), .Enable(Output_flag),
    .Ready(display_driver_1_ready), .High_nibble(display_driver_1_high_nibble),
    .Low_nibble(display_driver_1_low_nibble));
  Button Reset (.out(Reset_out));
  // Probe on display_driver_1_ready
endmodule
